# Fritzing sketch trabalho2 (saved by Fritzing 0.9.3b)
breadboards: 1

parts:
  Part1 = Arduino Uno (Rev3)
  hc-sr1 = hc-sr04
  LCD1 = LCD screen
  LED1 = smd LED [color="Red (633nm)" package="0805 [SMD]"]
  LED2 = smd LED [color="Red (633nm)" package="0805 [SMD]"]
  LED3 = smd LED [color="Red (633nm)" package="0805 [SMD]"]
  R1 = Resistor [tolerance=±5% resistance=220 package="1206 [SMD]"]
  R2 = Resistor [tolerance=±5% resistance=220 package="1206 [SMD]"]
  R3 = Resistor [tolerance=±5% resistance=220 package="1206 [SMD]"]

nets:
  N1: Part1.A3, R1.Pin_0
  N2: Part1.A4/SDA, R2.Pin_0
  N3: Part1.A5/SCL, R3.Pin_0
  N4: Part1.D8, hc-sr1.Echo
  N5: Part1.D9_PWM, LCD1.RS
  N6: Part1.D10_PWM/SS, LCD1.E
  N7: Part1.D13/SCK, hc-sr1.Trig
  N8: Part1.D4, LCD1.DB4
  N9: Part1.D5_PWM, LCD1.DB5
  N10: Part1.D6_PWM, LCD1.DB6
  N11: Part1.D7, LCD1.DB7
  5V: Part1.5V, hc-sr1.VCC, LCD1.VDD, LCD1.LED+
  GND: Part1.GND, hc-sr1.GND, LCD1.VSS, LCD1.V0, LCD1.R/W, LCD1.DB0, LCD1.DB1, LCD1.DB2, LCD1.DB3, LCD1.LED-
  N12: LED1.cathode, LED2.cathode, LED3.cathode
  N13: LED1.anode, R1.Pin_1
  N14: LED2.anode, R2.Pin_1
  N15: LED3.anode, R3.Pin_1
